// Logisim project fsm.circ as structural Verilog: 1 circuit, main circuit main
module main (
  input  Clock,
  input  X,
  output S1_prime,
  output S0_prime
);

  wire and_1_out, and_2_out, and_3_out, and_4_out, not_1_out, or_1_out;

  and and_1 (and_1_out, ~X, ~S1_prime, ~S0_prime);  // AND_Gate
  and and_2 (and_2_out, X, ~S1_prime, S0_prime);  // AND_Gate
  and and_3 (and_3_out, ~X, S1_prime, S0_prime);  // AND_Gate
  and and_4 (and_4_out, X, X, S1_prime, ~S0_prime);  // AND_Gate
  or or_1 (or_1_out, and_1_out, and_2_out, and_3_out, and_4_out);
  not not_1 (not_1_out, S0_prime);
  D_Flip_Flop d_ff_1 (.clk(Clock), .D(or_1_out), .Q(S1_prime));  // open: Qn, preset, en, reset
  D_Flip_Flop d_ff_2 (.clk(Clock), .D(not_1_out), .Q(S0_prime));  // open: Qn, preset, en, reset
endmodule
