// Logisim project trafficlight.circ as structural Verilog: 1 circuit, main circuit main
module main (
  input  in_1,
  input  TA,
  input  TB,
  output Lights,
  output out_5,
  output out_6,
  output out_7
);

  wire and_1_out, and_2_out, xor_1_out, xor_2_out;

  and and_1 (and_1_out, ~TB, ~TB, ~TA);  // AND_Gate
  and and_2 (and_2_out, TB, ~TB, ~TB);  // AND_Gate
  xor xor_1 (xor_1_out, TB, TB);
  xor xor_2 (xor_2_out, and_1_out, and_2_out);
  D_Flip_Flop d_ff_1 (.clk(in_1), .D(xor_1_out), .Q(TB));  // open: Qn, preset, en, reset
  D_Flip_Flop d_ff_2 (.clk(in_1), .D(xor_2_out), .Q(TB));  // open: Qn, preset, en, reset
  and and_3 (out_5, ~TB, TB);  // AND_Gate
  not not_1 (out_6, TB);
  and and_4 (out_7, TB, TB);

  assign Lights = TB;

  // Notes on the sheet:
  //   Ryan Ma
  //   Clock
  //   00 - Green
  //   01 - Yellow
  //   10 - Red
endmodule
