// Logisim project binaryadder.circ as structural Verilog: 3 circuits, main circuit main
module main (
  input  in_1,
  input  in_2,
  input  in_3,
  input  in_4,
  input  in_5,
  input  in_6,
  input  in_7,
  input  in_8,
  output out_9,
  output out_10,
  output out_11,
  output out_12
);

  wire full_adder_2_c, full_adder_3_c, half_adder_1_s;

  full_adder full_adder_1 (.A(in_1), .B(full_adder_2_c), .Cin(in_6), .S(out_9));  // open: C
  full_adder full_adder_2 (.A(in_2), .B(full_adder_3_c), .Cin(in_7), .C(full_adder_2_c), .S(out_10));
  full_adder full_adder_3 (.A(in_3), .B(half_adder_1_s), .Cin(in_8), .C(full_adder_3_c), .S(out_11));
  half_adder half_adder_1 (.A(in_4), .B(in_5), .S(half_adder_1_s), .C(out_12));

  // Notes on the sheet:
  //   Ryan Ma
endmodule

module half_adder (
  input  A,
  input  B,
  output S,
  output C
);

  or or_1 (S, A, B);
  and and_1 (C, A, B);
endmodule

module full_adder (
  input  A,
  input  B,
  input  Cin,
  output C,
  output S
);

  wire and_1_out, and_2_out, and_3_out, or_1_out;

  and and_1 (and_1_out, A, B);
  and and_2 (and_2_out, B, Cin);
  and and_3 (and_3_out, B, Cin);
  or or_1 (or_1_out, A, B, Cin);
  or or_2 (C, and_1_out, and_2_out, and_3_out);
  or or_3 (S, or_1_out, Cin);
endmodule
