// Logisim project decoder.circ as structural Verilog: 1 circuit, main circuit main
module main (
  input  in_1,
  input  Ryan_Ma,
  output out_3,
  output out_4,
  output out_5,
  output out_6
);

  wire not_1_out, not_2_out, not_3_out, not_4_out;

  not not_1 (not_1_out, in_1);
  not not_2 (not_2_out, Ryan_Ma);
  not not_3 (not_3_out, in_1);
  not not_4 (not_4_out, Ryan_Ma);
  and and_1 (out_3, not_1_out, not_2_out);
  and and_2 (out_4, not_3_out, Ryan_Ma);
  and and_3 (out_5, in_1, not_4_out);
  and and_4 (out_6, in_1, Ryan_Ma);
endmodule
